// Logisim project 1.circ as structural Verilog: 1 circuit, main circuit main
module main (
  input  A,
  input  B,
  input  C,
  output out_4
);

  wire A1_out, A1B1_out, A1B1C3_out, A1B1C_out, A1B_out, A1BC_out, AB_out, ABC1_out, B1_out, C1_out,
       or_1_out, or_2_out;

  and AB (AB_out, A, B);
  not A1 (A1_out, A);
  not B1 (B1_out, B);
  not C1 (C1_out, C);
  and ABC1 (ABC1_out, AB_out, C1_out);
  and A1B (A1B_out, A1_out, B);
  and A1B1 (A1B1_out, B1_out, A1_out);
  and A1BC (A1BC_out, A1B_out, C);
  and A1B1C (A1B1C_out, A1B1_out, C);
  and A1B1C3 (A1B1C3_out, C1_out, A1B1_out);
  or or_1 (or_1_out, ABC1_out, A1BC_out);
  or or_2 (or_2_out, or_1_out, A1B1C3_out);
  or F (out_4, or_2_out, A1B1C_out);
endmodule
