// Logisim project 2.circ as structural Verilog: 1 circuit, main circuit main
module main (
  input  A,
  input  B,
  input  C,
  output out_4
);

  wire AB1_out, AC1_out, B1_out, BC1_out, C1_out, or_1_out;

  not B1 (B1_out, B);
  not C1 (C1_out, C);
  and AB1 (AB1_out, A, B1_out);
  and BC1 (BC1_out, B, C1_out);
  and AC1 (AC1_out, C1_out, A);
  or or_1 (or_1_out, AB1_out, BC1_out);
  or F (out_4, or_1_out, AC1_out);
endmodule
