// Logisim project 3.circ as structural Verilog: 1 circuit, main circuit main
module main (
  input  A,
  input  B
);

  wire A1_out, A1B1_out, A1B_out, AB1_out, B1_out, F_out, or_1_out;

  not A1 (A1_out, A);
  not B1 (B1_out, B);
  and AB1 (AB1_out, A, B1_out);
  and A1B (A1B_out, A1_out, B);
  and A1B1 (A1B1_out, A1_out, B1_out);
  or or_1 (or_1_out, AB1_out, A1B_out);
  or F (F_out, or_1_out, A1B1_out);
  LED led_1 (.in(F_out));
endmodule
