// Logisim project 4.circ as structural Verilog: 1 circuit, main circuit main
module main (
  input  A,
  input  B,
  input  C,
  input  D
);

  wire A1B1_out, A1B1C1_out, A1B1C1D_out, AB_out, ABC1_out, ABC_out, ABCD_out, ABD_out, BC_out, BCD_out,
       F_out, not_1_out, not_2_out, not_3_out, or_1_out, or_2_out, or_3_out;

  not not_1 (not_1_out, A);
  not not_2 (not_2_out, B);
  not not_3 (not_3_out, C);
  and AB (AB_out, A, B);
  and A1B1 (A1B1_out, not_1_out, not_2_out);
  and BC (BC_out, C, B);
  and ABC1 (ABC1_out, AB_out, not_3_out);
  and A1B1C1 (A1B1C1_out, A1B1_out, not_3_out);
  and ABC (ABC_out, AB_out, C);
  and BCD (BCD_out, BC_out, D);
  and A1B1C1D (A1B1C1D_out, A1B1C1_out, D);
  and ABCD (ABCD_out, ABC_out, D);
  and ABD (ABD_out, AB_out, D);
  or or_1 (or_1_out, A1B1C1D_out, ABCD_out);
  or or_2 (or_2_out, BCD_out, ABD_out);
  or or_3 (or_3_out, ABC1_out, or_1_out);
  or F (F_out, or_3_out, or_2_out);
  LED led_1 (.in(F_out));
endmodule
