// Logisim project assignment1.circ as structural Verilog: 1 circuit, main circuit main
module main (
  input  in_1,
  input  Clr,
  output f,
  output e,
  output a,
  output b,
  output c,
  output d,
  output g
);

  wire and_1_out, and_2_out, and_3_out, and_4_out, and_5_out, and_6_out, and_7_out, and_8_out, and_9_out,
       clock_1_out, not_1_out, not_2_out, not_3_out, not_4_out, or_1_out, or_2_out, t_ff_1_q, t_ff_1_qn,
       t_ff_2_q, t_ff_3_q, t_ff_4_q;

  Clock clock_1 (.out(clock_1_out));
  T_Flip_Flop #(.trigger("falling")) t_ff_1 (
    .T(or_1_out), .clk(clock_1_out), .Q(t_ff_1_q), .Qn(t_ff_1_qn), .reset(Clr), .preset(in_1));
  or or_1 (or_1_out, and_1_out, t_ff_1_q);
  and and_1 (and_1_out, and_2_out, t_ff_2_q);
  T_Flip_Flop #(.trigger("falling")) t_ff_2 (
    .T(and_2_out), .clk(clock_1_out), .Q(t_ff_2_q), .reset(Clr), .preset(in_1));  // open: Qn
  T_Flip_Flop #(.trigger("falling")) t_ff_3 (
    .T(t_ff_4_q), .clk(clock_1_out), .Q(t_ff_3_q), .reset(Clr), .preset(in_1));  // open: Qn
  and and_2 (and_2_out, t_ff_4_q, t_ff_3_q);
  or or_2 (or_2_out, t_ff_3_q, t_ff_2_q, t_ff_1_qn, t_ff_4_q);
  T_Flip_Flop #(.trigger("falling")) t_ff_4 (
    .T(or_2_out), .clk(clock_1_out), .Q(t_ff_4_q), .reset(Clr), .preset(in_1));  // open: Qn
  not not_1 (not_1_out, t_ff_1_q);
  not not_2 (not_2_out, t_ff_2_q);
  not not_3 (not_3_out, t_ff_3_q);
  not not_4 (not_4_out, t_ff_4_q);
  and and_3 (and_3_out, not_1_out, not_2_out, not_3_out);
  and and_4 (and_4_out, not_2_out, t_ff_3_q);
  and and_5 (and_5_out, not_2_out, t_ff_4_q);
  and and_6 (and_6_out, not_1_out, not_2_out, not_4_out);
  and and_7 (and_7_out, t_ff_2_q, t_ff_3_q);
  and and_8 (and_8_out, not_4_out, t_ff_3_q);
  or or_3 (b, t_ff_3_q, t_ff_2_q, t_ff_1_q);
  or or_4 (c, t_ff_1_q, t_ff_2_q, t_ff_4_q);
  or or_5 (d, t_ff_3_q, not_2_out);
  or or_6 (f, and_3_out, and_7_out);
  or or_7 (e, and_6_out, and_7_out, and_8_out);
  and and_9 (and_9_out, not_2_out, not_3_out);
  or or_8 (g, t_ff_1_q, and_4_out, and_5_out);
  or or_9 (a, t_ff_3_q, and_9_out);
  _7_Segment_Display u_7_segment_display_1 (.g(g), .f(f), .a(a), .b(b), .e(e), .d(d), .c(c));  // open: dp

  // Notes on the sheet:
  //   ASSUMPTIONS:-
  //   'I' and 1 are the same.
  //   flip flop used: T
  //   Display shows: CS23I1003
endmodule
