// Logisim project bcdadderusingfulladder.circ as structural Verilog: 2 circuits, main circuit main
module main (
  input  [3:0] inpy,
  input  [3:0] inpx,
  input  Z,
  output S0,
  output C4,
  output S3,
  output S2,
  output S1
);

  wire and_1_out, and_2_out, and_3_out, and_4_out, and_5_out, and_6_out, and_7_out, and_8_out, or_2_out,
       or_3_out, or_4_out, xor_2_out, xor_4_out, xor_6_out, xor_8_out;

  or or_1 (C4, and_1_out, and_2_out);
  and and_1 (and_1_out, or_2_out, xor_2_out);
  xor xor_1 (S3, or_2_out, xor_2_out);
  xor xor_2 (xor_2_out, inpx[3], inpy[3]);
  and and_2 (and_2_out, inpx[3], inpy[3]);
  or or_2 (or_2_out, and_3_out, and_4_out);
  xor xor_3 (S2, or_3_out, xor_4_out);
  and and_3 (and_3_out, or_3_out, xor_4_out);
  xor xor_4 (xor_4_out, inpx[2], inpy[2]);
  and and_4 (and_4_out, inpx[2], inpy[2]);
  or or_3 (or_3_out, and_5_out, and_6_out);
  and and_5 (and_5_out, or_4_out, xor_6_out);
  xor xor_5 (S1, or_4_out, xor_6_out);
  xor xor_6 (xor_6_out, inpx[1], inpy[1]);
  and and_6 (and_6_out, inpx[1], inpy[1]);
  or or_4 (or_4_out, and_7_out, and_8_out);
  xor xor_7 (S0, Z, xor_8_out);
  and and_7 (and_7_out, Z, xor_8_out);
  xor xor_8 (xor_8_out, inpx[0], inpy[0]);
  and and_8 (and_8_out, inpx[0], inpy[0]);
endmodule

module fulladd (
  input  [3:0] in_1,
  input  [3:0] in_2,
  input  in_3,
  input  in_4,
  input  in_5
);

  wire and_1_out, and_2_out, main_1_c4;
  wire [2:2] or_1_out;
  wire [3:0] main_1_s0, main_2_s0;

  main main_1 (
    .inpy(in_1), .inpx(in_2), .Z(in_3), .S0(main_1_s0[0]), .C4(main_1_c4), .S3(main_1_s0[3]),
    .S2(main_1_s0[2]), .S1(main_1_s0[1]));
  and and_1 (and_1_out, main_1_s0[3], main_1_s0[1]);
  and and_2 (and_2_out, main_1_s0[3], main_1_s0[2]);
  or or_1 (or_1_out[2], main_1_c4, and_1_out, and_2_out);
  main main_2 (
    .inpy(main_1_s0), .inpx({in_5, {2{or_1_out[2]}}, in_5}), .Z(in_4), .S0(main_2_s0[0]), .S3(main_2_s0[3]),
    .S2(main_2_s0[2]), .S1(main_2_s0[1]));  // open: C4
  Hex_Digit_Display hex_digit_display_1 (.value({{3{in_5}}, or_1_out[2]}));  // open: dp
  Hex_Digit_Display hex_digit_display_2 (.value(main_2_s0));  // open: dp
endmodule
