// Logisim project binarytogrey.circ as structural Verilog: 1 circuit, main circuit main
module main (
  input  B0,
  input  B1,
  input  B2,
  input  B3
);

  wire [2:0] xor_3_out;

  xor xor_1 (xor_3_out[2], B0, B1);
  xor xor_2 (xor_3_out[1], B1, B2);
  xor xor_3 (xor_3_out[0], B2, B3);
  Hex_Digit_Display hex_digit_display_1 (.value({B0, xor_3_out}));  // open: dp
endmodule
