// Logisim project countertocounter2.circ as structural Verilog: 1 circuit, main circuit main
module main (
  input  in_1,
  input  in_2,
  input  S,
  input  in_4,
  input  in_5,
  input  in_6
);

  wire and_1_out, and_2_out, and_3_out, and_4_out, and_5_out, and_6_out, and_7_out, clock_1_out, clock_2_out,
       not_1_out, not_2_out, not_3_out, or_1_out, t_ff_2_qn, t_ff_3_qn;
  wire [2:0] t_ff_3_q;
  wire [3:0] D_q;

  Clock clock_1 (.out(clock_1_out));
  Clock clock_2 (.out(clock_2_out));
  and and_1 (and_1_out, and_4_out, D_q[2]);
  T_Flip_Flop #(.trigger("falling")) A (
    .T(and_1_out), .clk(clock_1_out), .Q(D_q[3]), .reset(in_6), .preset(in_5));  // open: Qn
  T_Flip_Flop #(.trigger("falling")) t_ff_1 (
    .T(and_2_out), .clk(clock_2_out), .Q(t_ff_3_q[2]), .reset(in_2), .preset(in_1));  // open: Qn
  Hex_Digit_Display hex_digit_display_1 (.value(D_q));  // open: dp
  T_Flip_Flop #(.trigger("falling")) B (
    .T(and_4_out), .clk(clock_1_out), .Q(D_q[2]), .reset(in_6), .preset(in_5));  // open: Qn
  and and_2 (and_2_out, and_6_out, t_ff_2_qn);
  T_Flip_Flop #(.trigger("falling")) t_ff_2 (
    .T(and_6_out), .clk(clock_2_out), .Q(t_ff_3_q[1]), .Qn(t_ff_2_qn), .reset(in_2), .preset(in_1));
  not not_1 (not_1_out, t_ff_3_q[1]);
  not not_2 (not_2_out, t_ff_3_q[0]);
  and and_3 (and_3_out, t_ff_3_q[0], t_ff_3_q[1], t_ff_3_q[2]);
  and and_4 (and_4_out, and_7_out, D_q[1]);
  and and_5 (and_5_out, t_ff_3_q[2], not_1_out, not_2_out);
  or or_1 (or_1_out, and_5_out, and_3_out);
  T_Flip_Flop #(.trigger("falling")) C (
    .T(and_7_out), .clk(clock_1_out), .Q(D_q[1]), .reset(in_6), .preset(in_5));  // open: Qn
  and and_6 (and_6_out, t_ff_3_qn, not_3_out);
  T_Flip_Flop #(.trigger("falling")) t_ff_3 (
    .T(not_3_out), .clk(clock_2_out), .Q(t_ff_3_q[0]), .Qn(t_ff_3_qn), .reset(in_2), .preset(in_1));
  not not_3 (not_3_out, S);
  and and_7 (and_7_out, or_1_out, D_q[0]);
  T_Flip_Flop #(.trigger("falling")) D (
    .T(or_1_out), .clk(clock_1_out), .Q(D_q[0]), .reset(in_6), .preset(in_5));  // open: Qn
  Hex_Digit_Display hex_digit_display_2 (.value({in_4, t_ff_3_q}));  // open: dp
endmodule
