// Logisim project lab3.1.circ as structural Verilog: 1 circuit, main circuit main
module main (
  input  [3:0] inpy,
  input  [3:0] inpx,
  input  Z,
  input  in_4,
  input  in_5,
  input  in_6,
  input  [3:0] in_7,
  input  [3:0] in_8,
  input  in_9,
  input  in_10,
  input  in_11,
  input  in_12
);

  wire and_1_out, and_2_out, and_3_out, and_4_out, and_5_out, and_6_out, and_7_out, and_8_out, and_9_out,
       and_10_out, and_11_out, and_12_out, and_13_out, and_14_out, and_15_out, and_16_out, or_3_out,
       or_4_out, or_5_out, or_6_out, or_7_out, or_8_out, xor_3_out, xor_4_out, xor_5_out, xor_8_out,
       xor_9_out, xor_10_out, xor_13_out, xor_14_out, xor_15_out, xor_18_out, xor_19_out, xor_20_out;
  wire [0:0] or_1_out, or_2_out;
  wire [3:0] xor_16_out, xor_17_out;

  or or_1 (or_1_out[0], and_1_out, and_3_out);
  and and_1 (and_1_out, or_3_out, xor_3_out);
  or or_2 (or_2_out[0], and_2_out, and_4_out);
  xor xor_1 (xor_16_out[3], or_3_out, xor_3_out);
  xor xor_2 (xor_17_out[3], or_4_out, xor_4_out);
  and and_2 (and_2_out, or_4_out, xor_4_out);
  xor xor_3 (xor_3_out, inpx[3], inpy[3]);
  and and_3 (and_3_out, inpx[3], inpy[3]);
  xor xor_4 (xor_4_out, xor_5_out, in_7[3]);
  and and_4 (and_4_out, xor_5_out, in_7[3]);
  or or_3 (or_3_out, and_5_out, and_7_out);
  xor xor_5 (xor_5_out, in_8[3], in_9);
  xor xor_6 (xor_16_out[2], or_5_out, xor_8_out);
  and and_5 (and_5_out, or_5_out, xor_8_out);
  or or_4 (or_4_out, and_6_out, and_8_out);
  xor xor_7 (xor_17_out[2], or_6_out, xor_9_out);
  and and_6 (and_6_out, or_6_out, xor_9_out);
  xor xor_8 (xor_8_out, inpx[2], inpy[2]);
  and and_7 (and_7_out, inpx[2], inpy[2]);
  xor xor_9 (xor_9_out, xor_10_out, in_7[2]);
  and and_8 (and_8_out, xor_10_out, in_7[2]);
  xor xor_10 (xor_10_out, in_8[2], in_9);
  or or_5 (or_5_out, and_9_out, and_11_out);
  Hex_Digit_Display hex_digit_display_1 (.value({in_4, in_5, in_6, or_1_out[0]}));  // open: dp
  and and_9 (and_9_out, or_7_out, xor_13_out);
  or or_6 (or_6_out, and_10_out, and_12_out);
  Hex_Digit_Display hex_digit_display_2 (.value({in_10, in_11, in_12, or_2_out[0]}));  // open: dp
  xor xor_11 (xor_16_out[1], or_7_out, xor_13_out);
  Hex_Digit_Display hex_digit_display_3 (.value(xor_16_out));  // open: dp
  xor xor_12 (xor_17_out[1], or_8_out, xor_14_out);
  and and_10 (and_10_out, or_8_out, xor_14_out);
  Hex_Digit_Display hex_digit_display_4 (.value(xor_17_out));  // open: dp
  xor xor_13 (xor_13_out, inpx[1], inpy[1]);
  and and_11 (and_11_out, inpx[1], inpy[1]);
  xor xor_14 (xor_14_out, xor_15_out, in_7[1]);
  and and_12 (and_12_out, xor_15_out, in_7[1]);
  or or_7 (or_7_out, and_13_out, and_15_out);
  xor xor_15 (xor_15_out, in_8[1], in_9);
  xor xor_16 (xor_16_out[0], Z, xor_18_out);
  and and_13 (and_13_out, Z, xor_18_out);
  or or_8 (or_8_out, and_14_out, and_16_out);
  xor xor_17 (xor_17_out[0], in_9, xor_19_out);
  and and_14 (and_14_out, in_9, xor_19_out);
  xor xor_18 (xor_18_out, inpx[0], inpy[0]);
  and and_15 (and_15_out, inpx[0], inpy[0]);
  xor xor_19 (xor_19_out, xor_20_out, in_7[0]);
  and and_16 (and_16_out, xor_20_out, in_7[0]);
  xor xor_20 (xor_20_out, in_8[0], in_9);
endmodule
