// Logisim project lab4.circ as structural Verilog
module main (
  input  D0,
  input  D1,
  input  D2,
  input  D3,
  output A,
  output B
);

  or or_1 (A, D2, D3);
  or or_2 (B, D1, D3);
endmodule

module Decoder38 (
  input  D0,
  input  D1,
  input  D2,
  input  D3,
  input  D4,
  input  D5,
  input  D6,
  input  D7,
  output A,
  output B,
  output C
);

  or or_1 (A, D4, D5, D6, D7);
  or or_2 (B, D2, D3, D6, D7);
  or or_3 (C, D1, D3, D5, D7);
endmodule

module Encoder38 (
  input  A1,
  input  B1,
  input  A0,
  input  B0,
  output AequalB,
  output AgreaterthanB,
  output AlessthanB
);

  wire and_1_out, and_2_out, and_3_out, and_4_out, and_6_out, and_7_out, not_1_out, not_2_out, not_3_out,
       not_4_out, xnor_1_out, xnor_2_out;

  not not_1 (not_1_out, A1);
  not not_2 (not_2_out, B1);
  not not_3 (not_3_out, A0);
  not not_4 (not_4_out, B0);
  and and_1 (and_1_out, B0, not_3_out);
  xnor xnor_1 (xnor_1_out, A1, B1);
  xnor xnor_2 (xnor_2_out, A0, B0);
  and and_2 (and_2_out, A0, not_4_out);
  and and_3 (and_3_out, not_1_out, B1);
  and and_4 (and_4_out, A1, not_2_out);
  and and_5 (AequalB, xnor_1_out, xnor_2_out);
  and and_6 (and_6_out, xnor_1_out, and_2_out);
  and and_7 (and_7_out, xnor_2_out, and_1_out);
  or or_1 (AgreaterthanB, and_4_out, and_6_out);
  or or_2 (AlessthanB, and_3_out, and_7_out);
endmodule

module encoder24 (
  input  in_1,
  input  in_2,
  input  in_3,
  input  in_4,
  input  in_5,
  input  in_6,
  input  in_7,
  input  in_8
);

  wire encoder38_1_aequalb, encoder38_1_agreaterthanb, encoder38_1_alessthanb, main_1_a, main_1_b, main_2_a,
       main_2_b;

  main main_1 (.D0(in_1), .D1(in_2), .D2(in_3), .D3(in_4), .A(main_1_a), .B(main_1_b));
  main main_2 (.D0(in_5), .D1(in_6), .D2(in_7), .D3(in_8), .A(main_2_a), .B(main_2_b));
  Encoder38 encoder38_1 (
    .A1(main_1_a), .B1(main_2_a), .A0(main_1_b), .B0(main_2_b), .AequalB(encoder38_1_aequalb),
    .AgreaterthanB(encoder38_1_agreaterthanb), .AlessthanB(encoder38_1_alessthanb));
  LED led_1 (.in(encoder38_1_aequalb));
  LED led_2 (.in(encoder38_1_agreaterthanb));
  LED led_3 (.in(encoder38_1_alessthanb));
endmodule
