// Logisim project lab5.circ as structural Verilog: 2 circuits, main circuit main
module main (
  input  G0,
  input  G1,
  input  G2,
  input  G3,
  output B0,
  output B1,
  output B2,
  output B4
);

  xor xor_1 (B1, G0, G1);
  xor xor_2 (B2, B1, G2);
  xor xor_3 (B4, B2, G3);

  assign B0 = G0;
endmodule

module greytobinary (
  input  G0,
  input  G1,
  input  G2,
  input  G3,
  output B0,
  output B1,
  output B2,
  output B4
);

  xor xor_1 (B1, G0, G1);
  xor xor_2 (B2, B1, G2);
  xor xor_3 (B4, B2, G3);

  assign B0 = G0;
endmodule
