// Logisim project lookahaedandcarry2.circ as structural Verilog: 1 circuit, main circuit main
module main (
  input  [3:0] X,
  input  [3:0] Y,
  input  C0,
  input  in_4,
  output out_5,
  output S3,
  output S2,
  output S1,
  output S0
);

  wire and_1_out, and_2_out, and_3_out, and_4_out, C1_out, C2_out, C3_out, G0_out, G1_out, G2_out, G3_out,
       P0_out, P1_out, P2_out, P3_out;

  xor P3 (P3_out, X[3], Y[3]);
  and G3 (G3_out, X[3], Y[3]);
  xor P2 (P2_out, X[2], Y[2]);
  and G2 (G2_out, X[2], Y[2]);
  xor P1 (P1_out, X[1], Y[1]);
  and G1 (G1_out, X[1], Y[1]);
  xor P0 (P0_out, X[0], Y[0]);
  and G0 (G0_out, X[0], Y[0]);
  and and_1 (and_1_out, P3_out, C3_out);
  and and_2 (and_2_out, P2_out, C2_out);
  and and_3 (and_3_out, P0_out, C0);
  or C3 (C3_out, and_2_out, G2_out);
  and and_4 (and_4_out, P1_out, C1_out);
  or C2 (C2_out, and_4_out, G1_out);
  or C1 (C1_out, and_3_out, G0_out);
  or C4 (out_5, and_1_out, G3_out);
  xor xor_1 (S3, P3_out, C3_out);
  xor xor_2 (S2, P2_out, C2_out);
  xor xor_3 (S1, P1_out, C1_out);
  xor xor_4 (S0, P0_out, C0);
endmodule
