// Logisim project lookaheadcarry.circ as structural Verilog: 1 circuit, main circuit main
module main (
  input  [3:0] X,
  input  [3:0] Y,
  input  C0,
  output out_4,
  output S3,
  output S2,
  output S1,
  output S0
);

  wire and_1_out, and_2_out, and_3_out, and_4_out, and_5_out, and_6_out, and_7_out, and_8_out, and_9_out,
       and_10_out, C1_out, C2_out, C3_out, G0_out, G1_out, G2_out, G3_out, P0_out, P1_out, P2_out, P3_out;

  and G3 (G3_out, X[3], Y[3]);
  xor P3 (P3_out, X[3], Y[3]);
  and G2 (G2_out, X[2], Y[2]);
  xor P2 (P2_out, X[2], Y[2]);
  and G1 (G1_out, X[1], Y[1]);
  xor P1 (P1_out, X[1], Y[1]);
  and G0 (G0_out, X[0], Y[0]);
  xor P0 (P0_out, X[0], Y[0]);
  and and_1 (and_1_out, P3_out, P2_out, G1_out);
  and and_2 (and_2_out, P3_out, P2_out, P1_out, C0, P0_out);
  and and_3 (and_3_out, P3_out, G2_out);
  and and_4 (and_4_out, P3_out, P2_out, P1_out, G0_out);
  and and_5 (and_5_out, P2_out, P1_out, G0_out);
  and and_6 (and_6_out, P2_out, P1_out, C0, P0_out);
  and and_7 (and_7_out, P2_out, G1_out);
  and and_8 (and_8_out, P1_out, C0, P0_out);
  and and_9 (and_9_out, P1_out, G0_out);
  or C1 (C1_out, G0_out, and_10_out);
  and and_10 (and_10_out, P0_out, C0);
  or C2 (C2_out, G1_out, and_8_out, and_9_out);
  or C3 (C3_out, G2_out, and_5_out, and_6_out, and_7_out);
  or C4 (out_4, and_1_out, and_3_out, G3_out, and_2_out, and_4_out);
  xor xor_1 (S3, C3_out, P3_out);
  xor xor_2 (S2, P2_out, C2_out);
  xor xor_3 (S1, P1_out, C1_out);
  xor xor_4 (S0, P0_out, C0);
endmodule
